# Fritzing sketch TinkurWash Wiring Diagram (saved by Fritzing 0.8.7b)
breadboards: 1

parts:
  Part1 = Arduino Uno (Rev3)
  LED1 = RGB LED (com. anode, rbg) [package="5 mm [THT]"]
  R2 = Resistor [tolerance=±5% resistance=220 package=THT]
  R4 = Resistor [tolerance=±5% resistance=220 package=THT]
  R5 = Resistor [tolerance=±5% resistance=220 package=THT]
  CC1 = Adafruit CC3000 Shield for Arduino
  ADXL1 = ADXL335 Accelerometer Breakout

nets:
  N1: Part1.D8, CC1.D8, CC1.WCS
  N2: Part1.D11_PWM/MOSI, CC1.D11
  N3: Part1.D12/MISO, CC1.D12
  N4: Part1.D13/SCK, CC1.D13
  N5: Part1.D3_PWM, CC1.D3
  N6: Part1.D4, CC1.D4
  N7: Part1.D5_PWM, CC1.D5
  N8: LED1.red_cathode, R2.Pin_0
  N9: LED1.common_anode, R4.Pin_0
  N10: LED1.green_cathode, R5.Pin_0
  N11: R2.Pin_1, CC1.D10
  N12: R4.Pin_1, CC1.D9
  N13: R5.Pin_1, CC1.D6
  N14: CC1.RST, CC1.D7
  5V: CC1.5V, ADXL1.Vin
  GND: CC1.GND, ADXL1.GND
  N15: CC1.A0, ADXL1.Zout
  N16: CC1.A1, ADXL1.Yout
  N17: CC1.A2, ADXL1.Xout

notes:
  CC3000 Adafruit WiFi Shield
  D8 to WCS WiFi; WSC to D10 cut w/ razor blade

custom parts:
  ADXL335 Accelerometer Breakout: ADXL335 Accelerometer Breakout board
